# Fritzing sketch ESP8266-NTP-Clock (saved by Fritzing 0.9.9b)
breadboards: 1

parts:
  ESP8266 = Adafruit HUZZAH ESP8266 Breakout [part_number=2471]
  LED1 = 7-SEGMENT-4DIGIT-YOUNGSUN [package=7-segment-4digit-youngsun-longpads]
  IC1 = IC, DIP package, 20 pins [chip_label=TM1637]
  R1 = Resistor [tolerance=±5% power=0.25 resistance=1k package=THT]
  R2 = Resistor [tolerance=±5% power=0.25 resistance=1k package=THT]

nets:
  N1: ESP8266.GND, IC1.pin1
  N2: ESP8266.VBat, IC1.pin16, R1.Pin_1, R2.Pin_1
  N3: ESP8266.#13, IC1.pin17, R2.Pin_0
  N4: ESP8266.#12, IC1.pin18, R1.Pin_0
  N5: LED1.DIG1, IC1.pin15
  N6: LED1.DIG2, IC1.pin14
  N7: LED1.D, IC1.pin5
  N8: LED1.E, IC1.pin6
  N9: LED1.DIG3, IC1.pin13
  N10: LED1.DIG4, IC1.pin12
  N11: LED1.F, IC1.pin7
  N12: LED1.C, IC1.pin4
  N13: LED1.A, IC1.pin2
  N14: LED1.G, IC1.pin8
  N15: LED1.B, IC1.pin3
